// Logisim project 3-11.circ as structural Verilog: 1 circuit, main circuit main
module main (
  input  PS,
  input  LS,
  input  RS,
  input  RR,
  output PL,
  output LL,
  output RL
);

  wire not_1_out, not_2_out, not_3_out, not_4_out, or_1_out, or_2_out;

  not not_1 (not_1_out, PS);
  not not_2 (not_2_out, LS);
  not not_3 (not_3_out, RS);
  not not_4 (not_4_out, RR);
  and and_1 (LL, not_1_out, LS, or_1_out);
  or or_1 (or_1_out, not_3_out, RR);
  and and_2 (RL, not_1_out, RS, or_2_out);
  or or_2 (or_2_out, not_2_out, not_4_out);

  assign PL = PS;
endmodule
