// Logisim project 3-28.circ as structural Verilog: 1 circuit, main circuit main
module main (
  input  A,
  input  B,
  input  C,
  input  D,
  output out_5,
  output out_6,
  output out_7,
  output out_8,
  output out_9,
  output out_10,
  output out_11,
  output out_12,
  output out_13,
  output out_14,
  output out_15,
  output out_16,
  output out_17,
  output out_18,
  output out_19,
  output out_20
);

  wire not_1_out;

  not not_1 (not_1_out, D);
  Decoder #(.select(3)) decoder_1 (
    .out0(out_5), .out1(out_6), .out2(out_7), .out3(out_8), .out4(out_9), .out5(out_10), .out6(out_11),
    .out7(out_12), .sel({C, B, A}), .en(not_1_out));
  Decoder #(.select(3)) decoder_2 (
    .out0(out_13), .out1(out_14), .out2(out_15), .out3(out_16), .out4(out_17), .out5(out_18), .out6(out_19),
    .out7(out_20), .sel({C, B, A}), .en(D));
endmodule
