// Logisim project 3-44.circ as structural Verilog: 1 circuit, main circuit main
module main (
  input  X,
  input  Y,
  input  Z,
  output F1,
  output F2,
  output F3
);

  wire decoder_1_out0, decoder_1_out2, decoder_1_out3, decoder_1_out5, decoder_1_out7;

  Decoder #(.select(3)) decoder_1 (
    .out0(decoder_1_out0), .out2(decoder_1_out2), .out3(decoder_1_out3), .out5(decoder_1_out5),
    .out7(decoder_1_out7), .sel({Z, Y, X}), .en(1'b1));  // open: out1, out4, out6
  or or_1 (F1, decoder_1_out0, decoder_1_out2, decoder_1_out7);
  or or_2 (F2, decoder_1_out0, decoder_1_out2, decoder_1_out3);
  or or_3 (F3, decoder_1_out0, decoder_1_out2, decoder_1_out5);
endmodule
