// Logisim project 3-59.circ as structural Verilog: 2 circuits, main circuit old
module old (
  input  [3:0] A,
  input  [3:0] B
);

  wire and_1_out, and_2_out, not_1_out, not_2_out, not_3_out, not_4_out, not_5_out, not_6_out, not_7_out,
       not_8_out;

  not not_1 (not_1_out, A[0]);
  not not_2 (not_2_out, A[1]);
  not not_3 (not_3_out, A[2]);
  not not_4 (not_4_out, A[3]);
  not not_5 (not_5_out, B[3]);
  not not_6 (not_6_out, B[2]);
  not not_7 (not_7_out, B[1]);
  not not_8 (not_8_out, B[0]);
  and and_1 (and_1_out, not_5_out, not_4_out);
  and and_2 (and_2_out, B[3], A[3]);
  // OR_Gate or_1 has open pins: in0=and_1_out, in1=and_2_out, out=open
endmodule

module main (
  input  [3:0] A,
  input  [3:0] B,
  output X
);

  wire not_1_out, not_2_out, not_3_out, not_4_out, or_1_out, or_2_out, or_3_out, or_4_out, or_5_out,
       or_6_out, or_7_out, or_8_out, or_9_out, or_10_out, or_11_out, or_12_out, or_13_out, or_14_out,
       or_15_out, or_16_out, or_17_out, or_18_out, or_19_out, or_20_out, or_21_out, or_22_out, or_23_out;

  not not_1 (not_1_out, A[3]);
  not not_2 (not_2_out, A[2]);
  not not_3 (not_3_out, A[1]);
  not not_4 (not_4_out, A[0]);
  or or_1 (or_1_out, B[3], B[2], B[1], B[0]);
  or or_2 (or_2_out, not_4_out, B[3], B[2], B[1]);
  or or_3 (or_3_out, not_3_out, B[3], B[2], B[1]);
  or or_4 (or_4_out, not_3_out, B[3], B[2], B[0]);
  or or_5 (or_5_out, not_3_out, not_4_out, B[3], B[2]);
  or or_6 (or_6_out, not_2_out, B[3], B[2]);
  or or_7 (or_7_out, not_2_out, B[3], B[1], B[0]);
  or or_8 (or_8_out, not_2_out, not_4_out, B[3], B[1]);
  or or_9 (or_9_out, not_2_out, not_3_out, B[3], B[1]);
  or or_10 (or_10_out, not_2_out, not_3_out, B[3], B[0]);
  or or_11 (or_11_out, not_2_out, not_3_out, not_4_out, B[3]);
  or or_12 (or_12_out, not_1_out, B[3]);
  or or_13 (or_13_out, not_1_out, B[2], B[1], B[0]);
  or or_14 (or_14_out, not_1_out, not_4_out, B[2], B[1]);
  or or_15 (or_15_out, not_1_out, not_3_out, B[2], B[1]);
  or or_16 (or_16_out, not_1_out, not_3_out, B[2], B[0]);
  or or_17 (or_17_out, not_1_out, not_3_out, not_4_out, B[2]);
  or or_18 (or_18_out, not_1_out, not_2_out, B[2]);
  or or_19 (or_19_out, not_1_out, not_2_out, B[1], B[0]);
  or or_20 (or_20_out, not_1_out, not_2_out, not_4_out, B[1]);
  or or_21 (or_21_out, not_1_out, not_2_out, not_3_out, B[1]);
  or or_22 (or_22_out, not_1_out, not_2_out, not_3_out, B[0]);
  or or_23 (or_23_out, not_1_out, not_2_out, not_3_out, not_4_out);
  and and_1 (X, or_1_out, or_2_out, or_3_out, or_4_out, or_5_out, or_6_out, or_7_out, or_8_out, or_9_out, or_10_out, or_11_out, or_12_out, or_13_out, or_14_out, or_15_out, or_16_out, or_17_out, or_18_out, or_19_out, or_20_out, or_21_out, or_22_out, or_23_out);
endmodule
